// Digital circuit CMP.dig as structural Verilog
module CMP (
  input  [3:0] Function,
  input  EN,
  input  [15:0] q,
  input  [15:0] r,
  output [15:0] p,
  output p_CLK
);

  wire [5:0] comparator_1_gt, comparator_2_gt;
  wire [15:0] driver_1_out, driver_2_out;

  assign driver_1_out = EN ? q : 16'bz;  // Driver driver_1
  assign driver_2_out = EN ? r : 16'bz;  // Driver driver_2
  Comparator #(.Bits(16)) comparator_1 (
    .a(driver_1_out), .b(driver_2_out), .gt(comparator_1_gt[2]), .eq(comparator_1_gt[0]),
    .lt(comparator_1_gt[3]));
  Comparator #(.Signed("true"), .Bits(16)) comparator_2 (
    .a(driver_1_out), .b(driver_2_out), .gt(comparator_2_gt[2]), .eq(comparator_2_gt[0]),
    .lt(comparator_2_gt[3]));
  or or_1 (comparator_1_gt[4], comparator_1_gt[0], comparator_1_gt[2]);
  or or_2 (comparator_1_gt[5], comparator_1_gt[0], comparator_1_gt[3]);
  or or_3 (comparator_2_gt[4], comparator_2_gt[0], comparator_2_gt[2]);
  or or_4 (comparator_2_gt[5], comparator_2_gt[0], comparator_2_gt[3]);
  not not_1 (comparator_1_gt[1], comparator_1_gt[0]);
  not not_2 (comparator_2_gt[1], comparator_2_gt[0]);
  Multiplexer #(.Selector_Bits(4), .Bits(16)) multiplexer_1 (
    .sel(Function), .in_0({{10{1'b0}}, comparator_1_gt}), .in_1({{10{1'b0}}, comparator_2_gt}),
    .in_2({16{1'b0}}), .in_3({16{1'b0}}), .in_4({16{1'b0}}), .in_5({16{1'b0}}), .in_6({16{1'b0}}),
    .in_7({16{1'b0}}), .in_8({16{1'b0}}), .in_9({16{1'b0}}), .in_10({16{1'b0}}), .in_11({16{1'b0}}),
    .in_12({16{1'b0}}), .in_13({16{1'b0}}), .in_14({16{1'b0}}), .in_15({16{1'b0}}), .out(p));

  assign p_CLK = EN;
endmodule
