// Digital circuit D-EN-Decoder.dig as structural Verilog
module D_EN_Decoder (
  input  [16:0] IN,
  output [16:0] DATA,
  output [16:0] EN
);

  // Pins of 16 and 17 bits meet at IN
  // Pins of 16 and 17 bits meet at {DATA[16], IN[15:0]}
  // Pins of 1 and 17 bits meet at {EN[16:1], IN[16]}

  assign DATA[15:0] = IN[15:0];
  assign EN[0] = IN[16];
endmodule
