// Digital circuit JMP.dig as structural Verilog
module JMP (
  input  [3:0] Function,
  input  EN,
  input  [15:0] I3_I4,
  input  [15:0] p,
  input  [15:0] q,
  input  [15:0] PROG_counter,
  output [15:0] PROG_jump_to,
  output PROG_jump_EN
);

  wire multiplexer_3_out;
  wire [15:0] add_1_s, multiplexer_1_out;

  Multiplexer #(.Bits(16)) multiplexer_1 (.sel(Function[1]), .in_0(I3_I4), .in_1(q), .out(multiplexer_1_out));
  Add #(.Bits(16)) add_1 (.a(multiplexer_1_out), .b(PROG_counter), .c_i(1'b0), .s(add_1_s));  // open: c_o
  Multiplexer #(.Bits(16), .Selector_Bits(4)) multiplexer_2 (
    .sel(Function), .in_0(multiplexer_1_out), .in_1(multiplexer_1_out), .in_2(multiplexer_1_out),
    .in_3(multiplexer_1_out), .in_4(add_1_s), .in_5(add_1_s), .in_6(add_1_s), .in_7(add_1_s),
    .in_8({16{1'b0}}), .in_9({16{1'b0}}), .in_10({16{1'b0}}), .in_11({16{1'b0}}), .in_12({16{1'b0}}),
    .in_13({16{1'b0}}), .in_14({16{1'b0}}), .in_15({16{1'b0}}), .out(PROG_jump_to));
  Multiplexer #(.Selector_Bits(4)) multiplexer_3 (
    .sel(Function), .in_0(1'b1), .in_1(p[0]), .in_2(1'b1), .in_3(p[0]), .in_4(1'b1), .in_5(p[0]),
    .in_6(1'b1), .in_7(p[0]), .in_8(1'b0), .in_9(1'b0), .in_10(1'b0), .in_11(1'b0), .in_12(1'b0),
    .in_13(1'b0), .in_14(1'b0), .in_15(1'b0), .out(multiplexer_3_out));
  and and_1 (PROG_jump_EN, EN, multiplexer_3_out);
endmodule
