// Digital circuit Opcode-Decoder.dig as structural Verilog
module Opcode_Decoder (
  input  [7:0] I1,
  input  EN,
  output [3:0] Function,
  output [3:0] Subset,
  output LOAD,
  output STORE,
  output ARITH,
  output ARITH_SIGNED,
  output CMP,
  output JMP
);

  Demultiplexer #(.Selector_Bits(4)) demultiplexer_1 (
    .sel(I1[7:4]), .in(EN), .out_0(LOAD), .out_1(STORE), .out_2(ARITH), .out_3(ARITH_SIGNED), .out_4(CMP),
    .out_5(JMP));  // open: out_6, out_7, out_8, out_9, out_10, out_11, out_12, out_13, out_14, out_15

  assign Function = I1[3:0];
  assign Subset = I1[7:4];
endmodule
