// Digital circuit Register.dig as structural Verilog
module Register (
  input  [15:0] DATA_IN,
  input  CLK,
  input  [7:0] p_addr,
  input  [7:0] q_addr,
  input  [7:0] r_addr,
  output [15:0] p,
  output [15:0] q,
  output [15:0] r,
  output [15:0] R0
);

  wire d_en_decoder_1_p3, d_en_decoder_2_p3, d_en_decoder_3_p3, d_en_decoder_4_p3, d_en_decoder_5_p3,
       d_en_decoder_6_p3, d_en_decoder_7_p3, d_en_decoder_8_p3, delay_1_out;
  wire [15:0] d_en_decoder_1_p2, d_en_decoder_2_p2, d_en_decoder_3_p2, d_en_decoder_4_p2, d_en_decoder_5_p2,
       d_en_decoder_6_p2, d_en_decoder_7_p2, d_en_decoder_8_p2, d_ff_2_q, d_ff_3_q, d_ff_4_q, d_ff_5_q,
       d_ff_6_q, d_ff_7_q, d_ff_8_q;
  wire [16:0] d_en_encoder_1_out, demultiplexer_1_out_0, demultiplexer_1_out_1, demultiplexer_1_out_2,
       demultiplexer_1_out_3, demultiplexer_1_out_4, demultiplexer_1_out_5, demultiplexer_1_out_6,
       demultiplexer_1_out_7;

  Delay #(.delayTime(20)) delay_1 (.in(CLK), .out(delay_1_out));
  D_EN_Encoder d_en_encoder_1 (.DATA(DATA_IN), .EN(delay_1_out), .OUT(d_en_encoder_1_out));
  Demultiplexer #(.Selector_Bits(4), .Bits(17)) demultiplexer_1 (
    .sel(p_addr[3:0]), .in(d_en_encoder_1_out), .out_0(demultiplexer_1_out_0), .out_1(demultiplexer_1_out_1),
    .out_2(demultiplexer_1_out_2), .out_3(demultiplexer_1_out_3), .out_4(demultiplexer_1_out_4),
    .out_5(demultiplexer_1_out_5), .out_6(demultiplexer_1_out_6), .out_7(demultiplexer_1_out_7));  // open: out_8, out_9, out_10, out_11, out_12, out_13, out_14, out_15
  // D_EN_Decoder d_en_decoder_1: pin names not known; wires that end beside it: demultiplexer_1_out_0, d_en_decoder_1_p2, d_en_decoder_1_p3
  // D_EN_Decoder d_en_decoder_2: pin names not known; wires that end beside it: demultiplexer_1_out_1, d_en_decoder_2_p2, d_en_decoder_2_p3
  // D_EN_Decoder d_en_decoder_3: pin names not known; wires that end beside it: demultiplexer_1_out_2, d_en_decoder_3_p2, d_en_decoder_3_p3
  // D_EN_Decoder d_en_decoder_4: pin names not known; wires that end beside it: demultiplexer_1_out_3, d_en_decoder_4_p2, d_en_decoder_4_p3
  // D_EN_Decoder d_en_decoder_5: pin names not known; wires that end beside it: demultiplexer_1_out_4, d_en_decoder_5_p2, d_en_decoder_5_p3
  // D_EN_Decoder d_en_decoder_6: pin names not known; wires that end beside it: demultiplexer_1_out_5, d_en_decoder_6_p2, d_en_decoder_6_p3
  // D_EN_Decoder d_en_decoder_7: pin names not known; wires that end beside it: demultiplexer_1_out_6, d_en_decoder_7_p2, d_en_decoder_7_p3
  // D_EN_Decoder d_en_decoder_8: pin names not known; wires that end beside it: demultiplexer_1_out_7, d_en_decoder_8_p2, d_en_decoder_8_p3
  D_FF #(.Bits(16)) d_ff_1 (.D(d_en_decoder_1_p2), .C(d_en_decoder_1_p3), .Q(R0));  // open: nQ
  D_FF #(.Bits(16)) d_ff_2 (.D(d_en_decoder_2_p2), .C(d_en_decoder_2_p3), .Q(d_ff_2_q));  // open: nQ
  D_FF #(.Bits(16)) d_ff_3 (.D(d_en_decoder_3_p2), .C(d_en_decoder_3_p3), .Q(d_ff_3_q));  // open: nQ
  D_FF #(.Bits(16)) d_ff_4 (.D(d_en_decoder_4_p2), .C(d_en_decoder_4_p3), .Q(d_ff_4_q));  // open: nQ
  D_FF #(.Bits(16)) d_ff_5 (.D(d_en_decoder_5_p2), .C(d_en_decoder_5_p3), .Q(d_ff_5_q));  // open: nQ
  D_FF #(.Bits(16)) d_ff_6 (.D(d_en_decoder_6_p2), .C(d_en_decoder_6_p3), .Q(d_ff_6_q));  // open: nQ
  D_FF #(.Bits(16)) d_ff_7 (.D(d_en_decoder_7_p2), .C(d_en_decoder_7_p3), .Q(d_ff_7_q));  // open: nQ
  D_FF #(.Bits(16)) d_ff_8 (.D(d_en_decoder_8_p2), .C(d_en_decoder_8_p3), .Q(d_ff_8_q));  // open: nQ
  Multiplexer #(.Selector_Bits(4), .Bits(16)) multiplexer_1 (
    .sel(p_addr[3:0]), .in_0(R0), .in_1(d_ff_2_q), .in_2(d_ff_3_q), .in_3(d_ff_4_q), .in_4(d_ff_5_q),
    .in_5(d_ff_6_q), .in_6(d_ff_7_q), .in_7(d_ff_8_q), .in_8({16{1'b0}}), .in_9({16{1'b0}}),
    .in_10({16{1'b0}}), .in_11({16{1'b0}}), .in_12({16{1'b0}}), .in_13({16{1'b0}}), .in_14({16{1'b0}}),
    .in_15({16{1'b0}}), .out(p));
  Multiplexer #(.Selector_Bits(4), .Bits(16)) multiplexer_2 (
    .sel(q_addr[3:0]), .in_0(R0), .in_1(d_ff_2_q), .in_2(d_ff_3_q), .in_3(d_ff_4_q), .in_4(d_ff_5_q),
    .in_5(d_ff_6_q), .in_6(d_ff_7_q), .in_7(d_ff_8_q), .in_8({16{1'b0}}), .in_9({16{1'b0}}),
    .in_10({16{1'b0}}), .in_11({16{1'b0}}), .in_12({16{1'b0}}), .in_13({16{1'b0}}), .in_14({16{1'b0}}),
    .in_15({16{1'b0}}), .out(q));
  Multiplexer #(.Selector_Bits(4), .Bits(16)) multiplexer_3 (
    .sel(r_addr[3:0]), .in_0(R0), .in_1(d_ff_2_q), .in_2(d_ff_3_q), .in_3(d_ff_4_q), .in_4(d_ff_5_q),
    .in_5(d_ff_6_q), .in_6(d_ff_7_q), .in_7(d_ff_8_q), .in_8({16{1'b0}}), .in_9({16{1'b0}}),
    .in_10({16{1'b0}}), .in_11({16{1'b0}}), .in_12({16{1'b0}}), .in_13({16{1'b0}}), .in_14({16{1'b0}}),
    .in_15({16{1'b0}}), .out(r));

  // Notes on the sheet:
  //   p: pin 1
  //   q: pin 2
  //   r: pin 3
endmodule
