// Digital circuit ARITHMETIC.dig as structural Verilog
module ARITHMETIC (
  input  [3:0] Function,
  input  EN,
  input  [15:0] q,
  input  [15:0] r,
  input  [7:0] I4,
  output [15:0] p,
  output p_CLK
);

  wire [3:0] driver_1_out;
  wire [15:0] add_1_s, add_2_s, and_1_out, barrelshifter_1_out, barrelshifter_2_out, barrelshifter_3_out,
       barrelshifter_4_out, bitextender_1_out, div_1_q, div_1_r, driver_2_out, driver_3_out, not_1_out,
       or_1_out, sub_1_s, xor_1_out;
  wire [31:0] mul_1_mul;

  assign driver_1_out = EN ? Function : 4'bz;  // Driver driver_1
  assign driver_2_out = EN ? q : 16'bz;  // Driver driver_2
  assign driver_3_out = EN ? r : 16'bz;  // Driver driver_3
  BitExtender bitextender_1 (.in(I4), .out(bitextender_1_out));
  assign and_1_out = driver_2_out & driver_3_out;  // And and_1, 16 bits wide
  assign or_1_out = driver_2_out | driver_3_out;  // Or or_1, 16 bits wide
  assign xor_1_out = driver_2_out ^ driver_3_out;  // XOr xor_1, 16 bits wide
  assign not_1_out = ~driver_2_out;  // Not not_1, 16 bits wide
  Add #(.Bits(16)) add_1 (.a(driver_2_out), .b(driver_3_out), .c_i(1'b0), .s(add_1_s));  // open: c_o
  Sub #(.Bits(16)) sub_1 (.a(driver_2_out), .b(driver_3_out), .c_i(1'b0), .s(sub_1_s));  // open: c_o
  Mul #(.Bits(16)) mul_1 (.a(driver_2_out), .b(driver_3_out), .mul(mul_1_mul));
  Div #(.Bits(16)) div_1 (.a(driver_2_out), .b(driver_3_out), .q(div_1_q), .r(div_1_r));
  BarrelShifter #(.Bits(16)) barrelshifter_1 (.in(driver_2_out), .shift(driver_3_out[4:0]), .out(barrelshifter_1_out));
  BarrelShifter #(.Bits(16), .direction("right")) barrelshifter_2 (
    .in(driver_2_out), .shift(driver_3_out[4:0]), .out(barrelshifter_2_out));
  BarrelShifter #(.Bits(16)) barrelshifter_3 (
    .in(driver_2_out), .shift(bitextender_1_out[4:0]), .out(barrelshifter_3_out));
  BarrelShifter #(.Bits(16), .direction("right")) barrelshifter_4 (
    .in(driver_2_out), .shift(bitextender_1_out[4:0]), .out(barrelshifter_4_out));
  Add #(.Bits(16)) add_2 (.a(driver_2_out), .b(bitextender_1_out), .c_i(1'b0), .s(add_2_s));  // open: c_o
  Multiplexer #(.Selector_Bits(4), .Bits(16)) multiplexer_1 (
    .sel(driver_1_out), .in_0(and_1_out), .in_1(or_1_out), .in_2(xor_1_out), .in_3(not_1_out),
    .in_4(add_1_s), .in_5(sub_1_s), .in_6(mul_1_mul[15:0]), .in_7(div_1_q), .in_8(div_1_r),
    .in_9(barrelshifter_1_out), .in_10(barrelshifter_2_out), .in_11(barrelshifter_3_out),
    .in_12(barrelshifter_4_out), .in_13(add_2_s), .in_14({16{1'b0}}), .in_15({16{1'b0}}), .out(p));

  assign p_CLK = EN;
endmodule
