// Digital circuit Control-Unit.dig as structural Verilog
module Control_Unit (
  input  [31:0] Instruction,
  input  CLK,
  input  [15:0] RAM_in,
  input  PROG_reset,
  output [15:0] R0,
  output [15:0] RAM_out,
  output RAM_CLK,
  output [15:0] RAM_addr,
  output [15:0] PROG_Counter,
  output [15:0] RBP,
  output [15:0] RSP
);

  wire arithmetic_1_p_clk, cmp_1_p_clk, d_en_decoder_1_p3, d_en_decoder_2_p2, d_en_decoder_2_p3,
       d_en_decoder_3_p3, delay_1_out, jmp_1_prog_jump_en, load_1_p_clk, not_1_out, opcode_decoder_1_arith,
       opcode_decoder_1_arith_signed, opcode_decoder_1_cmp, opcode_decoder_1_jmp, opcode_decoder_1_load,
       opcode_decoder_1_store, prog_counter_set, rs_ff_as_1_q, store_1_ram_clk;
  wire [3:0] opcode_decoder_1_function, opcode_decoder_1_subset;
  wire [15:0] arithmetic_1_p, cmp_1_p, d_en_decoder_1_p2, jmp_1_prog_jump_to, load_1_p, load_1_ram_addr,
       register_1_p7, register_1_p8, register_1_p9, store_1_ram_addr, store_1_ram_out;
  wire [16:0] d_en_decoder_2_p1, d_en_decoder_3_p1, d_en_encoder_2_out, d_en_encoder_3_out,
       d_en_encoder_4_out, d_en_encoder_5_out;

  // D_EN_Decoder d_en_decoder_1: pin names not known; wires that end beside it: prog_counter_set, d_en_decoder_1_p2, d_en_decoder_1_p3
  RS_FF_AS rs_ff_as_1 (.S(CLK), .R(1'b0), .Q(rs_ff_as_1_q));  // open: nQ
  Delay #(.delayTime(10)) delay_1 (.in(rs_ff_as_1_q), .out(delay_1_out));
  CounterPreset #(.Bits(16), .isProgramCounter("true")) counterpreset_1 (
    .en(delay_1_out), .C(not_1_out), .dir(1'b0), .in(d_en_decoder_1_p2), .ld(d_en_decoder_1_p3),
    .clr(PROG_reset), .out(PROG_Counter));  // open: ovf
  not not_1 (not_1_out, CLK);
  Opcode_Decoder opcode_decoder_1 (
    .I1(Instruction[31:24]), .EN(CLK), .Function(opcode_decoder_1_function),
    .Subset(opcode_decoder_1_subset), .LOAD(opcode_decoder_1_load), .STORE(opcode_decoder_1_store),
    .ARITH(opcode_decoder_1_arith), .ARITH_SIGNED(opcode_decoder_1_arith_signed), .CMP(opcode_decoder_1_cmp),
    .JMP(opcode_decoder_1_jmp));
  // D_EN_Decoder d_en_decoder_2: pin names not known; wires that end beside it: d_en_decoder_2_p1, d_en_decoder_2_p2, d_en_decoder_2_p3
  JMP jmp_1 (
    .Function(opcode_decoder_1_function), .EN(opcode_decoder_1_jmp), .I3_I4(Instruction[15:0]),
    .p(register_1_p7), .q(register_1_p8), .PROG_counter(PROG_Counter), .PROG_jump_to(jmp_1_prog_jump_to),
    .PROG_jump_EN(jmp_1_prog_jump_en));
  CMP cmp_1 (
    .Function(opcode_decoder_1_function), .EN(opcode_decoder_1_cmp), .q(register_1_p8), .r(register_1_p9),
    .p(cmp_1_p), .p_CLK(cmp_1_p_clk));
  ARITHMETIC arithmetic_1 (
    .Function(opcode_decoder_1_function), .EN(opcode_decoder_1_arith), .q(register_1_p8), .r(register_1_p9),
    .I4(Instruction[7:0]), .p(arithmetic_1_p), .p_CLK(arithmetic_1_p_clk));
  STORE store_1 (
    .Function(opcode_decoder_1_function), .EN(opcode_decoder_1_store), .I2(Instruction[23:16]),
    .I3_I4(Instruction[15:0]), .p(register_1_p7), .q(register_1_p8), .RAM_out(store_1_ram_out),
    .RAM_CLK(store_1_ram_clk), .RAM_addr(store_1_ram_addr));
  LOAD load_1 (
    .Function(opcode_decoder_1_function), .EN(opcode_decoder_1_load), .I3_I4(Instruction[15:0]),
    .q(register_1_p8), .RAM_in(RAM_in), .p(load_1_p), .p_CLK(load_1_p_clk), .RAM_addr(load_1_ram_addr));
  // Register register_1: pin names not known; wires that end beside it: d_en_decoder_2_p2, d_en_decoder_2_p3, Instruction[23:16], Instruction[15:8], Instruction[7:0], PROG_Counter, register_1_p7, register_1_p8, register_1_p9, R0, RBP, RSP
  // D_EN_Encoder d_en_encoder_1: pin names not known; wires that end beside it: jmp_1_prog_jump_to, jmp_1_prog_jump_en, prog_counter_set
  D_EN_Encoder d_en_encoder_2 (.DATA(cmp_1_p), .EN(cmp_1_p_clk), .OUT(d_en_encoder_2_out));
  D_EN_Encoder d_en_encoder_3 (.DATA(arithmetic_1_p), .EN(arithmetic_1_p_clk), .OUT(d_en_encoder_3_out));
  D_EN_Encoder d_en_encoder_4 (.DATA(store_1_ram_out), .EN(store_1_ram_clk), .OUT(d_en_encoder_4_out));
  D_EN_Encoder d_en_encoder_5 (.DATA(load_1_p), .EN(load_1_p_clk), .OUT(d_en_encoder_5_out));
  Multiplexer #(.Selector_Bits(4), .Bits(17)) multiplexer_1 (
    .sel(opcode_decoder_1_subset), .in_0(d_en_encoder_5_out), .in_1({17{1'b0}}), .in_2(d_en_encoder_3_out),
    .in_3({17{1'b0}}), .in_4(d_en_encoder_2_out), .in_5({17{1'b0}}), .in_6({17{1'b0}}), .in_7({17{1'b0}}),
    .in_8({17{1'b0}}), .in_9({17{1'b0}}), .in_10({17{1'b0}}), .in_11({17{1'b0}}), .in_12({17{1'b0}}),
    .in_13({17{1'b0}}), .in_14({17{1'b0}}), .in_15({17{1'b0}}), .out(d_en_decoder_2_p1));
  Multiplexer #(.Selector_Bits(4), .Bits(16)) multiplexer_2 (
    .sel(opcode_decoder_1_subset), .in_0(load_1_ram_addr), .in_1(store_1_ram_addr), .in_2({16{1'b0}}),
    .in_3({16{1'b0}}), .in_4({16{1'b0}}), .in_5({16{1'b0}}), .in_6({16{1'b0}}), .in_7({16{1'b0}}),
    .in_8({16{1'b0}}), .in_9({16{1'b0}}), .in_10({16{1'b0}}), .in_11({16{1'b0}}), .in_12({16{1'b0}}),
    .in_13({16{1'b0}}), .in_14({16{1'b0}}), .in_15({16{1'b0}}), .out(RAM_addr));
  // D_EN_Decoder d_en_decoder_3: pin names not known; wires that end beside it: d_en_decoder_3_p1, RAM_out, d_en_decoder_3_p3
  Multiplexer #(.Selector_Bits(4), .Bits(17)) multiplexer_3 (
    .sel(opcode_decoder_1_subset), .in_0({17{1'b0}}), .in_1(d_en_encoder_4_out), .in_2({17{1'b0}}),
    .in_3({17{1'b0}}), .in_4({17{1'b0}}), .in_5({17{1'b0}}), .in_6({17{1'b0}}), .in_7({17{1'b0}}),
    .in_8({17{1'b0}}), .in_9({17{1'b0}}), .in_10({17{1'b0}}), .in_11({17{1'b0}}), .in_12({17{1'b0}}),
    .in_13({17{1'b0}}), .in_14({17{1'b0}}), .in_15({17{1'b0}}), .out(d_en_decoder_3_p1));
  Delay #(.delayTime(20)) delay_2 (.in(d_en_decoder_3_p3), .out(RAM_CLK));

  // Other names for the same wires on the sheet: prog_counter_val[15:0] = PROG_Counter

  // Notes on the sheet:
  //   PROG_Counter: The program counter. Specifies the memory address of the next instruction of the IMEM/program memory.
  //   PROG_reset: Resets the program counter if set to 1.
  //   Delay with a flip flop, so the
  //   first time the clock activates,
  //   the program counter is not
  //   incremented.
endmodule
