// Digital circuit LOAD.dig as structural Verilog
module LOAD (
  input  [3:0] Function,
  input  EN,
  input  [15:0] I3_I4,
  input  [15:0] q,
  input  [15:0] RAM_in,
  output [15:0] p,
  output p_CLK,
  output [15:0] RAM_addr
);

  wire delay_1_out;
  wire [15:0] add_1_s, bitextender_1_out;

  Delay #(.delayTime(10)) delay_1 (.in(EN), .out(delay_1_out));
  BitExtender bitextender_1 (.in(I3_I4[7:0]), .out(bitextender_1_out));
  Add #(.Bits(16)) add_1 (.a(q), .b(bitextender_1_out), .c_i(1'b0), .s(add_1_s));  // open: c_o
  Multiplexer #(.Selector_Bits(4), .Bits(16)) multiplexer_1 (
    .sel(Function), .in_0({16{1'b0}}), .in_1(I3_I4), .in_2(q), .in_3(RAM_in), .in_4(RAM_in),
    .in_5({16{1'b0}}), .in_6({16{1'b0}}), .in_7({16{1'b0}}), .in_8({16{1'b0}}), .in_9({16{1'b0}}),
    .in_10({16{1'b0}}), .in_11({16{1'b0}}), .in_12({16{1'b0}}), .in_13({16{1'b0}}), .in_14({16{1'b0}}),
    .in_15({16{1'b0}}), .out(p));
  Multiplexer #(.Selector_Bits(4)) multiplexer_2 (
    .sel(Function), .in_0(1'b0), .in_1(delay_1_out), .in_2(delay_1_out), .in_3(delay_1_out),
    .in_4(delay_1_out), .in_5(delay_1_out), .in_6(1'b0), .in_7(1'b0), .in_8(1'b0), .in_9(1'b0), .in_10(1'b0),
    .in_11(1'b0), .in_12(1'b0), .in_13(1'b0), .in_14(1'b0), .in_15(1'b0), .out(p_CLK));
  Multiplexer #(.Selector_Bits(4), .Bits(16)) multiplexer_3 (
    .sel(Function), .in_0({16{1'b0}}), .in_1({16{1'b0}}), .in_2({16{1'b0}}), .in_3(I3_I4), .in_4(add_1_s),
    .in_5({16{1'b0}}), .in_6({16{1'b0}}), .in_7({16{1'b0}}), .in_8({16{1'b0}}), .in_9({16{1'b0}}),
    .in_10({16{1'b0}}), .in_11({16{1'b0}}), .in_12({16{1'b0}}), .in_13({16{1'b0}}), .in_14({16{1'b0}}),
    .in_15({16{1'b0}}), .out(RAM_addr));
endmodule
