// Digital circuit Main.dig as structural Verilog
module Main (
  input  clk,
  output [15:0] out_1,
  output [15:0] out_2,
  output [15:0] out_4,
  output [15:0] out_5,
  output [31:0] out_6
);

  wire button_1_out, control_unit_1_ram_clk, DOWN_out, or_1_out;
  wire [15:0] control_unit_1_ram_addr, control_unit_1_ram_out, ramdualport_1_d;
  wire [31:0] rom_1_d;

  ROM #(.AddrBits(16), .Bits(32)) rom_1 (.A(out_2), .sel(1'b1), .D(rom_1_d));
  Button DOWN (.out(DOWN_out));
  or or_1 (or_1_out, clk, DOWN_out);
  D_FF #(.Bits(32)) d_ff_1 (.D(rom_1_d), .C(or_1_out), .Q(out_6));  // open: nQ
  Control_Unit control_unit_1 (
    .Instruction(out_6), .CLK(or_1_out), .RAM_in(ramdualport_1_d), .PROG_reset(button_1_out), .R0(out_1),
    .RAM_out(control_unit_1_ram_out), .RAM_CLK(control_unit_1_ram_clk), .RAM_addr(control_unit_1_ram_addr),
    .PROG_Counter(out_2), .RBP(out_4), .RSP(out_5));
  Button button_1 (.out(button_1_out));
  RAMDualPort #(.AddrBits(16), .Bits(16)) ramdualport_1 (
    .A(control_unit_1_ram_addr), .Din(control_unit_1_ram_out), .str(1'b1), .C(control_unit_1_ram_clk),
    .ld(1'b1), .D(ramdualport_1_d));

  // Notes on the sheet:
  //   clk: Hz: 5000
  //   contents of rom_1 (hex, n*v repeats v):
  //   2d0d0d01,1000009,12000d00,2000f00,2d000005,2d0d0d01,12000d00,5000000a
  //   ,2000c00,50000049,2d0d0d01,120e0d00,20e0d00,4000efe,1030001,1040000
  //   ,40010003,40020004,21010102,51010015,50000017,10c0001,50000036
  //   ,4000efe,2d0000ff,2d0d0d01,12000d00,2000f00,2d000005,2d0d0d01
  //   ,12000d00,5000000a,2d0d0dff,2d0d0d01,120c0d00,4000efe,2d0000fe
  //   ,2d0d0d01,12000d00,2000f00,2d000005,2d0d0d01,12000d00,5000000a
  //   ,2d0d0dff,2d0d0d01,120c0d00,4030d00,2d0d0dff,4040d00,2d0d0dff
  //   ,10c0000,240c0304,50000036,20d0e00,40e0d00,2d0d0dff,4000d00,2d0d0dff
  //   ,52000000,2d0d0d01,120e0d00,20e0d00,2d0e0eff,4000efe,4010efd,240c0001
  //   ,20d0e00,40e0d00,2d0d0dff,40d0d00,2d0d0dff,52000000,50000049
endmodule
