// Digital circuit Register.dig as structural Verilog
module Register (
  input  [15:0] DATA_IN,
  input  CLK,
  input  [7:0] p_addr,
  input  [7:0] q_addr,
  input  [7:0] r_addr,
  input  [15:0] prog_counter,
  output [15:0] p,
  output [15:0] q,
  output [15:0] r,
  output [15:0] R0
);

  wire d_en_decoder_1_p3, d_en_decoder_2_p3, d_en_decoder_3_p3, d_en_decoder_4_p3, d_en_decoder_5_p4,
       d_en_decoder_6_p3, d_en_decoder_7_p3, d_en_decoder_8_p3, d_en_decoder_9_p3, d_en_decoder_10_p3,
       d_en_decoder_11_p3, d_en_decoder_12_p3, d_en_decoder_13_p3, d_en_decoder_14_p3, d_en_decoder_15_p3,
       delay_1_out;
  wire [15:0] d_en_decoder_1_p2, d_en_decoder_2_p2, d_en_decoder_3_p2, d_en_decoder_4_p2, d_en_decoder_5_p3,
       d_en_decoder_6_p2, d_en_decoder_7_p2, d_en_decoder_8_p2, d_en_decoder_9_p2, d_en_decoder_10_p2,
       d_en_decoder_11_p2, d_en_decoder_12_p2, d_en_decoder_13_p2, d_en_decoder_14_p2, d_en_decoder_15_p2,
       d_ff_2_q, d_ff_3_q, d_ff_4_q, d_ff_5_q, d_ff_6_q, d_ff_7_q, d_ff_8_q, d_ff_9_q, d_ff_10_q, d_ff_11_q,
       d_ff_12_q, d_ff_13_q, d_ff_14_q, d_ff_15_q;
  wire [16:0] d_en_encoder_1_out, demultiplexer_1_out_0, demultiplexer_1_out_1, demultiplexer_1_out_2,
       demultiplexer_1_out_3, demultiplexer_1_out_4, demultiplexer_1_out_5, demultiplexer_1_out_6,
       demultiplexer_1_out_7, demultiplexer_1_out_8, demultiplexer_1_out_9, demultiplexer_1_out_10,
       demultiplexer_1_out_11, demultiplexer_1_out_12, demultiplexer_1_out_13, demultiplexer_1_out_14,
       demultiplexer_1_out_15;

  Delay #(.delayTime(20)) delay_1 (.in(CLK), .out(delay_1_out));
  D_EN_Encoder d_en_encoder_1 (.DATA(DATA_IN), .EN(delay_1_out), .OUT(d_en_encoder_1_out));
  Demultiplexer #(.Selector_Bits(4), .Bits(17)) demultiplexer_1 (
    .sel(p_addr[3:0]), .in(d_en_encoder_1_out), .out_0(demultiplexer_1_out_0), .out_1(demultiplexer_1_out_1),
    .out_2(demultiplexer_1_out_2), .out_3(demultiplexer_1_out_3), .out_4(demultiplexer_1_out_4),
    .out_5(demultiplexer_1_out_5), .out_6(demultiplexer_1_out_6), .out_7(demultiplexer_1_out_7),
    .out_8(demultiplexer_1_out_8), .out_9(demultiplexer_1_out_9), .out_10(demultiplexer_1_out_10),
    .out_11(demultiplexer_1_out_11), .out_12(demultiplexer_1_out_12), .out_13(demultiplexer_1_out_13),
    .out_14(demultiplexer_1_out_14), .out_15(demultiplexer_1_out_15));
  // D_EN_Decoder d_en_decoder_1: pin names not known; wires that end beside it: demultiplexer_1_out_0, d_en_decoder_1_p2, d_en_decoder_1_p3
  // D_EN_Decoder d_en_decoder_2: pin names not known; wires that end beside it: demultiplexer_1_out_1, d_en_decoder_2_p2, d_en_decoder_2_p3
  // D_EN_Decoder d_en_decoder_3: pin names not known; wires that end beside it: demultiplexer_1_out_2, d_en_decoder_3_p2, d_en_decoder_3_p3
  // D_EN_Decoder d_en_decoder_4: pin names not known; wires that end beside it: demultiplexer_1_out_3, d_en_decoder_4_p2, d_en_decoder_4_p3
  // D_EN_Decoder d_en_decoder_5: pin names not known; wires that end beside it: demultiplexer_1_out_15, demultiplexer_1_out_4, d_en_decoder_5_p3, d_en_decoder_5_p4
  // D_EN_Decoder d_en_decoder_6: pin names not known; wires that end beside it: demultiplexer_1_out_5, d_en_decoder_6_p2, d_en_decoder_6_p3
  // D_EN_Decoder d_en_decoder_7: pin names not known; wires that end beside it: demultiplexer_1_out_6, d_en_decoder_7_p2, d_en_decoder_7_p3
  // D_EN_Decoder d_en_decoder_8: pin names not known; wires that end beside it: demultiplexer_1_out_7, d_en_decoder_8_p2, d_en_decoder_8_p3
  // D_EN_Decoder d_en_decoder_9: pin names not known; wires that end beside it: demultiplexer_1_out_8, d_en_decoder_9_p2, d_en_decoder_9_p3
  // D_EN_Decoder d_en_decoder_10: pin names not known; wires that end beside it: demultiplexer_1_out_9, d_en_decoder_10_p2, d_en_decoder_10_p3
  // D_EN_Decoder d_en_decoder_11: pin names not known; wires that end beside it: demultiplexer_1_out_10, d_en_decoder_11_p2, d_en_decoder_11_p3
  // D_EN_Decoder d_en_decoder_12: pin names not known; wires that end beside it: demultiplexer_1_out_11, d_en_decoder_12_p2, d_en_decoder_12_p3
  // D_EN_Decoder d_en_decoder_13: pin names not known; wires that end beside it: demultiplexer_1_out_12, d_en_decoder_13_p2, d_en_decoder_13_p3
  // D_EN_Decoder d_en_decoder_14: pin names not known; wires that end beside it: demultiplexer_1_out_13, d_en_decoder_14_p2, d_en_decoder_14_p3
  // D_EN_Decoder d_en_decoder_15: pin names not known; wires that end beside it: demultiplexer_1_out_14, d_en_decoder_15_p2, d_en_decoder_15_p3
  D_FF #(.Bits(16)) d_ff_1 (.D(d_en_decoder_1_p2), .C(d_en_decoder_1_p3), .Q(R0));  // open: nQ
  D_FF #(.Bits(16)) d_ff_2 (.D(d_en_decoder_2_p2), .C(d_en_decoder_2_p3), .Q(d_ff_2_q));  // open: nQ
  D_FF #(.Bits(16)) d_ff_3 (.D(d_en_decoder_3_p2), .C(d_en_decoder_3_p3), .Q(d_ff_3_q));  // open: nQ
  D_FF #(.Bits(16)) d_ff_4 (.D(d_en_decoder_4_p2), .C(d_en_decoder_4_p3), .Q(d_ff_4_q));  // open: nQ
  D_FF #(.Bits(16)) d_ff_5 (.D(d_en_decoder_5_p3), .C(d_en_decoder_5_p4), .Q(d_ff_5_q));  // open: nQ
  D_FF #(.Bits(16)) d_ff_6 (.D(d_en_decoder_6_p2), .C(d_en_decoder_6_p3), .Q(d_ff_6_q));  // open: nQ
  D_FF #(.Bits(16)) d_ff_7 (.D(d_en_decoder_7_p2), .C(d_en_decoder_7_p3), .Q(d_ff_7_q));  // open: nQ
  D_FF #(.Bits(16)) d_ff_8 (.D(d_en_decoder_8_p2), .C(d_en_decoder_8_p3), .Q(d_ff_8_q));  // open: nQ
  D_FF #(.Bits(16)) d_ff_9 (.D(d_en_decoder_9_p2), .C(d_en_decoder_9_p3), .Q(d_ff_9_q));  // open: nQ
  D_FF #(.Bits(16)) d_ff_10 (.D(d_en_decoder_10_p2), .C(d_en_decoder_10_p3), .Q(d_ff_10_q));  // open: nQ
  D_FF #(.Bits(16)) d_ff_11 (.D(d_en_decoder_11_p2), .C(d_en_decoder_11_p3), .Q(d_ff_11_q));  // open: nQ
  D_FF #(.Bits(16)) d_ff_12 (.D(d_en_decoder_12_p2), .C(d_en_decoder_12_p3), .Q(d_ff_12_q));  // open: nQ
  D_FF #(.Bits(16)) d_ff_13 (.D(d_en_decoder_13_p2), .C(d_en_decoder_13_p3), .Q(d_ff_13_q));  // open: nQ
  D_FF #(.Bits(16)) d_ff_14 (.D(d_en_decoder_14_p2), .C(d_en_decoder_14_p3), .Q(d_ff_14_q));  // open: nQ
  D_FF #(.Bits(16)) d_ff_15 (.D(d_en_decoder_15_p2), .C(d_en_decoder_15_p3), .Q(d_ff_15_q));  // open: nQ
  Multiplexer #(.Selector_Bits(4), .Bits(16)) multiplexer_1 (
    .sel(p_addr[3:0]), .in_0(R0), .in_1(d_ff_2_q), .in_2(d_ff_3_q), .in_3(d_ff_4_q), .in_4(d_ff_5_q),
    .in_5(d_ff_6_q), .in_6(d_ff_7_q), .in_7(d_ff_8_q), .in_8(d_ff_9_q), .in_9(d_ff_10_q), .in_10(d_ff_11_q),
    .in_11(d_ff_12_q), .in_12(d_ff_13_q), .in_13(d_ff_14_q), .in_14(d_ff_15_q), .in_15(prog_counter), .out(p));
  Multiplexer #(.Selector_Bits(4), .Bits(16)) multiplexer_2 (
    .sel(q_addr[3:0]), .in_0(R0), .in_1(d_ff_2_q), .in_2(d_ff_3_q), .in_3(d_ff_4_q), .in_4(d_ff_5_q),
    .in_5(d_ff_6_q), .in_6(d_ff_7_q), .in_7(d_ff_8_q), .in_8(d_ff_9_q), .in_9(d_ff_10_q), .in_10(d_ff_11_q),
    .in_11(d_ff_12_q), .in_12(d_ff_13_q), .in_13(d_ff_14_q), .in_14(d_ff_15_q), .in_15(prog_counter), .out(q));
  Multiplexer #(.Selector_Bits(4), .Bits(16)) multiplexer_3 (
    .sel(r_addr[3:0]), .in_0(R0), .in_1(d_ff_2_q), .in_2(d_ff_3_q), .in_3(d_ff_4_q), .in_4(d_ff_5_q),
    .in_5(d_ff_6_q), .in_6(d_ff_7_q), .in_7(d_ff_8_q), .in_8(d_ff_9_q), .in_9(d_ff_10_q), .in_10(d_ff_11_q),
    .in_11(d_ff_12_q), .in_12(d_ff_13_q), .in_13(d_ff_14_q), .in_14(d_ff_15_q), .in_15(prog_counter), .out(r));

  // Notes on the sheet:
  //   p: pin 1
  //   q: pin 2
  //   r: pin 3
endmodule
