// Digital circuit STORE.dig as structural Verilog
module STORE (
  input  [3:0] Function,
  input  EN,
  input  [7:0] I2,
  input  [15:0] I3_I4,
  input  [15:0] p,
  input  [15:0] q,
  output [15:0] RAM_out,
  output RAM_CLK,
  output [15:0] RAM_addr
);

  wire [3:0] driver_1_out;
  wire [15:0] add_1_s, bitextender_1_out;

  Multiplexer #(.Selector_Bits(4), .Bits(16)) multiplexer_1 (
    .sel(driver_1_out), .in_0({{8{1'b0}}, I2}), .in_1(p), .in_2({16{1'b0}}), .in_3({16{1'b0}}),
    .in_4({16{1'b0}}), .in_5({16{1'b0}}), .in_6({16{1'b0}}), .in_7({16{1'b0}}), .in_8({16{1'b0}}),
    .in_9({16{1'b0}}), .in_10({16{1'b0}}), .in_11({16{1'b0}}), .in_12({16{1'b0}}), .in_13({16{1'b0}}),
    .in_14({16{1'b0}}), .in_15({16{1'b0}}), .out(RAM_out));
  assign driver_1_out = EN ? Function : 4'bz;  // Driver driver_1
  BitExtender bitextender_1 (.in(I3_I4[7:0]), .out(bitextender_1_out));
  Add #(.Bits(16)) add_1 (.a(q), .b(bitextender_1_out), .c_i(1'b0), .s(add_1_s));  // open: c_o
  Multiplexer #(.Selector_Bits(4), .Bits(16)) multiplexer_2 (
    .sel(Function), .in_0({16{1'b0}}), .in_1(I3_I4), .in_2(add_1_s), .in_3({16{1'b0}}), .in_4({16{1'b0}}),
    .in_5({16{1'b0}}), .in_6({16{1'b0}}), .in_7({16{1'b0}}), .in_8({16{1'b0}}), .in_9({16{1'b0}}),
    .in_10({16{1'b0}}), .in_11({16{1'b0}}), .in_12({16{1'b0}}), .in_13({16{1'b0}}), .in_14({16{1'b0}}),
    .in_15({16{1'b0}}), .out(RAM_addr));

  assign RAM_CLK = EN;
endmodule
